// Logisim project TP1.circ as structural Verilog: 1 circuit, main circuit main
module main (
  input  Exercice_1,
  input  in_2,
  input  in_3,
  input  in_4,
  input  in_5,
  output out_6,
  output out_7,
  output out_8
);

  wire transistor_5_out;

  Pull_Resistor #(.pull(1)) pull_resistor_1 (.node(out_6));
  Transistor transistor_1 (.in(1'b0), .out(out_6), .gate(Exercice_1));
  Pull_Resistor #(.pull(1)) pull_resistor_2 (.node(out_7));
  Pull_Resistor #(.pull(1)) pull_resistor_3 (.node(out_8));
  Transistor #(.\type ("n")) transistor_2 (.in(1'b0), .out(out_7), .gate(in_2));
  Transistor #(.\type ("n"), .gate("br")) transistor_3 (.in(1'b0), .out(out_7), .gate(in_3));
  Transistor #(.\type ("n")) transistor_4 (.in(transistor_5_out), .out(out_8), .gate(in_4));
  Transistor #(.\type ("n")) transistor_5 (.in(1'b0), .out(transistor_5_out), .gate(in_5));

  // Notes on the sheet:
  //   Exercice 2
endmodule
