// Logisim project TP1Exo3.circ as structural Verilog: 1 circuit, main circuit main
module main (
  input  a,
  input  b,
  output out_3
);

  wire pull_resistor_1_node, pull_resistor_4_node, transistor_1_out;

  Pull_Resistor #(.pull(1)) pull_resistor_1 (.node(pull_resistor_1_node));
  Transistor transistor_1 (.in(pull_resistor_4_node), .out(transistor_1_out), .gate(a));
  Pull_Resistor #(.pull(1)) pull_resistor_2 (.node(transistor_1_out));
  Transistor #(.\type ("n")) transistor_2 (.in(b), .out(pull_resistor_1_node), .gate(transistor_1_out));
  Pull_Resistor #(.pull(1)) pull_resistor_3 (.node(out_3));
  Pull_Resistor pull_resistor_4 (.node(pull_resistor_4_node));
  Transistor #(.\type ("n")) transistor_3 (.in(1'b0), .out(out_3), .gate(pull_resistor_1_node));
  Transistor #(.\type ("n"), .gate("br")) transistor_4 (.in(1'b0), .out(out_3), .gate(b));
  Transistor transistor_5 (.in(1'b0), .out(pull_resistor_4_node), .gate(b));
  Pull_Resistor #(.pull(1)) pull_resistor_5 (.node(pull_resistor_4_node));
endmodule
