// Logisim project TP1Exo5.circ as structural Verilog: 1 circuit, main circuit main
module main (
  input  a,
  input  b,
  input  c,
  input  d,
  output out_5
);

  wire transistor_2_out, transistor_3_out, transistor_4_out, transistor_5_out, transistor_6_out,
       transistor_8_out;

  Transistor transistor_1 (.in(1'b0), .out(out_5), .gate(a));
  Transistor transistor_2 (.in(1'b0), .out(transistor_2_out), .gate(c));
  Transistor #(.\type ("n")) transistor_3 (.in(transistor_2_out), .out(transistor_3_out), .gate(c));
  Transistor transistor_4 (.in(1'b0), .out(transistor_4_out), .gate(d));
  Transistor #(.\type ("n")) transistor_5 (.in(out_5), .out(transistor_5_out), .gate(a));
  Pull_Resistor pull_resistor_1 (.node(transistor_5_out));
  Pull_Resistor pull_resistor_2 (.node(transistor_3_out));
  Transistor transistor_6 (.in(transistor_4_out), .out(transistor_6_out), .gate(d));
  Pull_Resistor pull_resistor_3 (.node(transistor_6_out));
  Transistor transistor_7 (.in(1'b0), .out(out_5), .gate(b));
  Transistor #(.\type ("n")) transistor_8 (.in(out_5), .out(transistor_8_out), .gate(b));
  Pull_Resistor pull_resistor_4 (.node(transistor_8_out));
endmodule
