// Logisim project exercice1.circ as structural Verilog: 1 circuit, main circuit main
module main (
  input  i,
  input  s,
  output r0,
  output r1
);

  wire not_1_out;

  not not_1 (not_1_out, s);
  and and_1 (r1, i, s);
  and and_2 (r0, i, not_1_out);
endmodule
