// Logisim project exercice2.circ as structural Verilog: 1 circuit, main circuit main
module main (
  input  x1,
  input  x0,
  input  y1,
  input  y0,
  input  s,
  output r1,
  output r0
);

  Multiplexer #(.enable("false")) multiplexer_1 (.in0(x1), .in1(y1), .out(r1), .sel(s));
  Multiplexer #(.enable("false")) multiplexer_2 (.in0(x0), .in1(y0), .out(r0), .sel(s));
endmodule
