// Logisim project exercice4.circ as structural Verilog: 1 circuit, main circuit main
module main (
  input  h,
  input  g,
  input  f,
  input  e,
  input  d,
  input  c,
  input  b,
  input  a,
  input  s2,
  input  s1,
  input  s0,
  output r
);

  wire multiplexer_1_out, multiplexer_2_out, multiplexer_3_out, multiplexer_4_out, multiplexer_5_out,
       multiplexer_6_out;

  Multiplexer #(.enable("false")) multiplexer_1 (.in0(a), .in1(b), .out(multiplexer_1_out), .sel(s2));
  Multiplexer #(.enable("false")) multiplexer_2 (.in0(c), .in1(d), .out(multiplexer_2_out), .sel(s2));
  Multiplexer #(.enable("false")) multiplexer_3 (.in0(e), .in1(f), .out(multiplexer_3_out), .sel(s2));
  Multiplexer #(.enable("false")) multiplexer_4 (.in0(g), .in1(h), .out(multiplexer_4_out), .sel(s2));
  Multiplexer #(.enable("false")) multiplexer_5 (
    .in0(multiplexer_1_out), .in1(multiplexer_2_out), .out(multiplexer_5_out), .sel(s1));
  Multiplexer #(.enable("false")) multiplexer_6 (
    .in0(multiplexer_3_out), .in1(multiplexer_4_out), .out(multiplexer_6_out), .sel(s1));
  Multiplexer #(.enable("false")) multiplexer_7 (.in0(multiplexer_5_out), .in1(multiplexer_6_out), .out(r), .sel(s0));
endmodule
