// Logisim project exercice5.circ as structural Verilog: 1 circuit, main circuit main
module main (
  input  x,
  input  y,
  input  z,
  input  t,
  input  [1:0] in_5,
  input  [1:0] in_6,
  output out_7
);

  wire multiplexer_1_out, multiplexer_2_out;

  Multiplexer #(.select(2), .enable("false")) multiplexer_1 (
    .in0(x), .in1(y), .in2(z), .in3(t), .out(multiplexer_1_out), .sel(in_6));
  Multiplexer #(.select(2), .enable("false")) multiplexer_2 (
    .in0(x), .in1(y), .in2(z), .in3(t), .out(multiplexer_2_out), .sel(in_5));
  and and_1 (out_7, multiplexer_1_out, multiplexer_2_out);
endmodule
