// Logisim project exercice6.circ as structural Verilog: 1 circuit, main circuit main
module main (
  input  ci,
  input  a,
  input  b,
  output r,
  output co
);

  wire and_1_out, and_2_out, xor_1_out;

  and and_1 (and_1_out, a, b);
  or or_1 (co, and_1_out, and_2_out);
  xor xor_1 (xor_1_out, a, b);
  and and_2 (and_2_out, ci, xor_1_out);
  xor xor_2 (r, ci, xor_1_out);
endmodule
