// Logisim project exercice7.circ as structural Verilog: 1 circuit, main circuit main
module main (
  input  ci,
  input  [1:0] in_2,
  input  [1:0] in_3,
  output [1:0] out_4,
  output out_5
);

  wire and_1_out, and_2_out, and_3_out, and_4_out, or_1_out, xor_1_out, xor_2_out;

  and and_1 (and_1_out, in_3[0], in_2[0]);
  or or_1 (or_1_out, and_1_out, and_3_out);
  and and_2 (and_2_out, in_3[1], in_2[1]);
  xor xor_1 (xor_1_out, in_3[0], in_2[0]);
  and and_3 (and_3_out, ci, xor_1_out);
  xor xor_2 (xor_2_out, in_3[1], in_2[1]);
  and and_4 (and_4_out, or_1_out, xor_2_out);
  or or_2 (out_5, and_2_out, and_4_out);
  xor xor_3 (out_4[0], ci, xor_1_out);
  xor xor_4 (out_4[1], or_1_out, xor_2_out);

  // Notes on the sheet:
  //   co
  //   r
  //   r
endmodule
