// Logisim project exercice8.circ as structural Verilog: 1 circuit, main circuit main
module main (
  input  i1,
  input  i0
);

  wire and_1_out, and_2_out, not_1_out, not_2_out, or_1_out;

  not not_1 (not_1_out, i1);
  not not_2 (not_2_out, i0);
  and and_1 (and_1_out, not_1_out, i0);
  and and_2 (and_2_out, i1, not_2_out);
  or or_1 (or_1_out, and_1_out, and_2_out);
  // RGBLED rgbled_1: pin names not known; wires that end beside it: i1, or_1_out, 1'b0
endmodule
