// Logisim project Exo1.circ as structural Verilog: 1 circuit, main circuit main
module main (
  input  neg,
  input  in_2,
  input  in_3,
  input  in_4,
  input  in_5,
  output out_6,
  output out_7,
  output out_8,
  output out_9
);

  wire and_1_out, and_2_out, and_3_out, and_4_out, and_5_out, and_6_out, and_7_out, and_8_out, not_1_out,
       not_2_out, not_3_out, not_4_out, not_5_out, not_6_out, not_7_out, not_8_out;

  and and_1 (and_1_out, in_2, neg);
  not not_1 (not_1_out, in_2);
  and and_2 (and_2_out, not_1_out, not_2_out);
  not not_2 (not_2_out, neg);
  and and_3 (and_3_out, in_3, neg);
  not not_3 (not_3_out, in_3);
  and and_4 (and_4_out, not_3_out, not_4_out);
  not not_4 (not_4_out, neg);
  and and_5 (and_5_out, in_4, neg);
  not not_5 (not_5_out, in_4);
  and and_6 (and_6_out, not_5_out, not_6_out);
  not not_6 (not_6_out, neg);
  and and_7 (and_7_out, in_5, neg);
  not not_7 (not_7_out, in_5);
  and and_8 (and_8_out, not_7_out, not_8_out);
  not not_8 (not_8_out, neg);
  or or_1 (out_6, and_1_out, and_2_out);
  or or_2 (out_7, and_3_out, and_4_out);
  or or_3 (out_8, and_5_out, and_6_out);
  or or_4 (out_9, and_7_out, and_8_out);
endmodule
