// Logisim project exo2.circ as structural Verilog: 1 circuit, main circuit main
module main (
  input  Ci,
  input  x,
  input  y,
  output r,
  output Co
);

  wire and_1_out, and_2_out, xor_1_out;

  and and_1 (and_1_out, x, y);
  xor xor_1 (xor_1_out, x, y);
  or or_1 (Co, and_1_out, and_2_out);
  and and_2 (and_2_out, Ci, xor_1_out);
  xor xor_2 (r, Ci, xor_1_out);
endmodule
